# Fritzing sketch wiring_diagram (saved by Fritzing 0.9.2b)
breadboards: 1

parts:
  Part2 = Bluetooth HC-05 Macho  # not connected
  Part1 = Arduino Uno (Rev3)
  S1 = Reed switch [package=THT]
  CONN1 = USB connector [package=THT]  # not connected
  Power_plug1 = Power plug  # not connected
  Raspberry_Pi1 = Raspberry Pi 2  # not connected

nets:
  N1: Part1.D3_PWM, S1.pin_2
  N2: Part1.GND, S1.pin_1
